# Fritzing sketch gps_i2c (saved by Fritzing 0.9.4)
breadboards: 1

parts:
  Part1 = Adafruit Ultimate GPS v3 [part_number="Adafruit #746"]
  Part2 = Adafruit Pi T-Cobbler [part_number="Adafruit #1754 and #1105"]

nets:
  N1: Part1.1PPS, Part2.GPIO#4
  VIN: Part1.VIN, Part2.3.3V
  GND: Part1.GND, Part2.GND
  N2: Part1.RX, Part2.TXD
  N3: Part1.TX, Part2.RXD

custom parts:
  Adafruit Ultimate GPS v3: We carry a few different GPS modules here in the Adafruit shop, but none that satisfied our every desire - that's why we designed this little GPS breakout board. We believe this is the Ultimate GPS module, so we named it that. It's got everything you want and more: -165 dBm sensitivity, 10 Hz updates, 66 channels 5V friendly design and only 20mA current draw Breadboard friendly + two mounting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
  Adafruit Pi T-Cobbler: Now that you've finally got your hands on a Raspberry Pi® , you're probably itching to make some fun embedded computer projects with it. What you need is an assembled add on prototyping Pi T-Cobbler from Adafruit, which can break out all those tasty power, GPIO, I2C and SPI pins from the 26 pin header onto a solderless breadboard. This mini kit will make "cobbling together" prototypes with the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
